// Digital circuit and_dia.dig as structural Verilog
module and_dia (
  input  a,
  input  b,
  output out
);

  wire nand_1_out;

  nand nand_1 (nand_1_out, a, b);
  not not_1 (out, nand_1_out);
endmodule
