// Digital circuit mux_dia.dig as structural Verilog
module mux_dia (
  input  a,
  input  b,
  input  sel,
  output out
);

  wire and_1_out, and_2_out, not_1_out;

  and and_1 (and_1_out, not_1_out, a);
  and and_2 (and_2_out, b, sel);
  not not_1 (not_1_out, sel);
  xor xor_1 (out, and_1_out, and_2_out);
endmodule
