// Digital circuit or_dia.dig as structural Verilog
module or_dia (
  input  a,
  input  b,
  output out
);

  wire and_1_out, not_1_out, not_2_out;

  not not_1 (not_1_out, a);
  not not_2 (not_2_out, b);
  and and_1 (and_1_out, not_1_out, not_2_out);
  not not_3 (out, and_1_out);
endmodule
