// Digital circuit dmux4way_dia.dig as structural Verilog
module dmux4way_dia (
  input  in,
  input  sel_1,
  input  sel_0,
  output a,
  output b,
  output c,
  output d
);

  wire demultiplexer_1_out_0, demultiplexer_1_out_1;

  Demultiplexer demultiplexer_1 (.sel(sel_1), .in(in), .out_0(demultiplexer_1_out_0), .out_1(demultiplexer_1_out_1));
  Demultiplexer demultiplexer_2 (.sel(sel_0), .in(demultiplexer_1_out_0), .out_0(a), .out_1(b));
  Demultiplexer demultiplexer_3 (.sel(sel_0), .in(demultiplexer_1_out_1), .out_0(c), .out_1(d));
endmodule
