// Digital circuit mux4way16_dia.dig as structural Verilog
module mux4way16_dia (
  input  a,
  input  b,
  input  c,
  input  d,
  input  sel_1,
  input  sel_0,
  output out
);

  wire multiplexer_1_out, multiplexer_2_out;

  Multiplexer multiplexer_1 (.sel(sel_0), .in_0(a), .in_1(b), .out(multiplexer_1_out));
  Multiplexer multiplexer_2 (.sel(sel_0), .in_0(c), .in_1(d), .out(multiplexer_2_out));
  Multiplexer multiplexer_3 (.sel(sel_1), .in_0(multiplexer_1_out), .in_1(multiplexer_2_out), .out(out));
endmodule
